# Fritzing sketch ledmatrix (saved by Fritzing 0.9.0b)
circuit board: 8.46667cm x 5.64444cm
breadboards: 1

parts:
  R1 = Resistor [tolerance=±5% resistance=220 package=THT]
  LED1 = LED - 5mm [color="Red (633nm)" package="5 mm [THT]"]
  V1 = DC Power [voltage=5]
  U1 = atmega328 [package=dip]
  S3 = Pushbutton [package="[SMD]"]
  R2 = Resistor [tolerance=±5% resistance=10k package=THT]
  C1 = Electrolytic Capacitor [capacitance=10µF package="100 mil [THT, electrolytic]"]
  XTAL1 = Crystal [frequency="16 Mhz" package=THT]
  R3 = Resistor [tolerance=±5% resistance=220 package=THT]
  LED2 = LED - 5mm [color="Yellow (595nm)" package="5 mm [THT]"]
  C2 = Ceramic Capacitor [capacitance="100 nF" package="1206 [SMD, multilayer]"]
  C3 = Ceramic Capacitor [capacitance="100 nF" package="1206 [SMD, multilayer]"]

nets:
  N1: R1.Pin_0, LED1.anode
  N2: R1.Pin_1, V1.V+, U1.VCC, U1.AVCC, S3.Pin_3, S3.Pin_4, R2.Pin_1, C1.+, LED2.cathode
  N3: LED1.cathode, V1.V-, U1.GND, C1.-, C2.1, C3.0
  N4: U1.RESET, S3.Pin_1, S3.Pin_2, R2.Pin_0
  N5: U1.XLAT1, XTAL1.pin_0, C3.1
  N6: U1.XLAT2, XTAL1.pin_1, C2.0
  N7: U1.D13, R3.Pin_0
  N8: R3.Pin_1, LED2.anode
